# Fritzing sketch tree-v2 (saved by Fritzing 0.9.3b)
breadboards: 1

parts:
  WeMos_D1_Mini1 = WeMos D1 Mini
  C1 = Capacitor Polarized [package=cpol-radial-1000uf-25v]
  IC1 = IC, DIP package, 20 pins [chip_label=SN74HCT245N]
  R1 = Resistor [tolerance=±5% resistance=220 package="0805 [SMD]"]
  Part1 = ws2812b [package="smd 2812b"]
  IR1 = TSOP312.., 314.. [package=THT]

nets:
  5V: WeMos_D1_Mini1.5V, C1.+, IC1.pin20, Part1.VDD, IR1.Vs
  N1: WeMos_D1_Mini1.D6, IR1.Data
  N2: WeMos_D1_Mini1.D7, IC1.pin18
  VSS: WeMos_D1_Mini1.G, C1.-, IC1.pin1, IC1.pin3, IC1.pin4, IC1.pin5, IC1.pin6, IC1.pin7, IC1.pin8, IC1.pin9, IC1.pin10, IC1.pin11, IC1.pin12, IC1.pin13, IC1.pin14, IC1.pin15, IC1.pin16, IC1.pin17, IC1.pin19, Part1.VSS, IR1.GND
  N3: IC1.pin2, R1.Pin_0
  N4: R1.Pin_1, Part1.DIN

custom parts:
  WeMos D1 Mini: The D1 mini is a mini wifi board based on ESP-8266EX.
